# Fritzing sketch CO2-sensor-unit (saved by Fritzing 1.0.1rc)
breadboards: 1

parts:
  M1 = Arduino NANO RP2040 CONNECT with headers
  Part7 = Digital Temperature Sensor Breakout - TMP102

nets:
  N1: M1.GND-4, M1.GND-29, Part7.GND
  N2: M1.+3V3, Part7.V+
  N3: M1.D18, Part7.SDA
  N4: M1.D19, Part7.SCL
