# Fritzing sketch first-prototype (saved by Fritzing 1.0.1rc)
breadboards: 1

parts:
  Part7 = Digital Temperature Sensor Breakout - TMP102
  Mod1 = Raspberry Pi Pico W

nets:
  N1: Part7.V+, Mod1.pin_36
  N2: Part7.SDA, Mod1.pin_21
  N3: Part7.SCL, Mod1.pin_22
  N4: Part7.GND, Mod1.pin_3, Mod1.pin_8, Mod1.pin_13, Mod1.pin_18, Mod1.pin_23, Mod1.pin_28, Mod1.pin_33, Mod1.pin_38

custom parts:
  Raspberry Pi Pico W: Raspberry Pi Pico W. Based around the RP2040 microcontroller the Pico W is a low cost microcontroller device bringing Raspberry Pi quality, cost, and easy of use to the microcontroller space. The areas marked KEEPOUT in pcb silkscreen should not have traces running through them to avoid shorts on a soldered in module!
